// Logisim project EP02.circ as structural Verilog: 4 circuits, main circuit ULA 74LS181
module ULA_74LS181 (
  input  [3:0] in_1,
  input  [3:0] in_2,
  input  [3:0] in_3,
  output [3:0] out_4
);

  wire [3:0] and_1_out, and_2_out, and_3_out, nand_1_out, nor_1_out, not_1_out, not_2_out, not_3_out,
       not_4_out, not_5_out, not_6_out, not_7_out, or_1_out, or_2_out, or_3_out, xor_1_out, xor_2_out;

  assign not_1_out = ~in_2;  // NOT_Gate not_1, 4 bits wide
  assign not_2_out = ~in_1;  // NOT_Gate not_2, 4 bits wide
  assign not_3_out = ~in_2;  // NOT_Gate not_3, 4 bits wide
  assign and_1_out = not_1_out & in_1;  // AND_Gate and_1, 4 bits wide
  assign nand_1_out = ~(in_2 & in_2);  // NAND_Gate nand_1, 4 bits wide
  assign not_4_out = ~in_1;  // NOT_Gate not_4, 4 bits wide
  assign xor_1_out = in_2 ^ in_1;  // XOR_Gate xor_1, 4 bits wide
  assign and_2_out = in_2 & not_2_out;  // AND_Gate and_2, 4 bits wide
  assign not_5_out = ~in_2;  // NOT_Gate not_5, 4 bits wide
  assign or_1_out = not_5_out | in_1;  // OR_Gate or_1, 4 bits wide
  assign not_6_out = ~xor_2_out;  // NOT_Gate not_6, 4 bits wide
  assign xor_2_out = in_2 ^ in_1;  // XOR_Gate xor_2, 4 bits wide
  assign and_3_out = in_2 & in_1;  // AND_Gate and_3, 4 bits wide
  assign or_2_out = in_2 | not_7_out;  // OR_Gate or_2, 4 bits wide
  assign not_7_out = ~in_1;  // NOT_Gate not_7, 4 bits wide
  assign nor_1_out = ~(in_2 | in_1);  // NOR_Gate nor_1, 4 bits wide
  assign or_3_out = in_2 | in_1;  // OR_Gate or_3, 4 bits wide
  Multiplexer #(.select(4), .width(4), .enable("false")) multiplexer_1 (
    .in0(not_3_out), .in1(nor_1_out), .in2(and_1_out), .in3(4'b0000), .in4(nand_1_out), .in5(not_4_out),
    .in6(xor_1_out), .in7(and_2_out), .in8(or_1_out), .in9(not_6_out), .in10(in_1), .in11(and_3_out),
    .in12(4'b0001), .in13(or_2_out), .in14(or_3_out), .in15(in_2), .out(out_4), .sel(in_3));
endmodule

module ULA_1_bit (
  input  Carry_in,
  input  [1:0] Operation,
  input  A,
  input  B,
  input  Binvert,
  output Result,
  output CarryOut
);

  wire and_1_out, multiplexer_1_out, not_1_out, not_2_out, or_1_out, somador_1_out_4;

  Multiplexer #(.enable("false")) multiplexer_1 (.in0(B), .in1(not_1_out), .out(multiplexer_1_out), .sel(Binvert));
  not not_1 (not_1_out, B);
  and and_1 (and_1_out, A, multiplexer_1_out);
  or or_1 (or_1_out, A, multiplexer_1_out);
  not not_2 (not_2_out, A);
  somador somador_1 (.A(A), .B(multiplexer_1_out), .in_1(Carry_in), .out_5(CarryOut), .out_4(somador_1_out_4));
  Multiplexer #(.select(2), .enable("false")) multiplexer_2 (
    .in0(and_1_out), .in1(or_1_out), .in2(not_2_out), .in3(somador_1_out_4), .out(Result), .sel(Operation));
endmodule

module somador (
  input  in_1,
  input  A,
  input  B,
  output out_4,
  output out_5
);

  wire and_1_out, and_2_out, xor_1_out;

  and and_1 (and_1_out, B, A);
  xor xor_1 (xor_1_out, A, B);
  xor xor_2 (out_5, and_1_out, and_2_out);
  xor xor_3 (out_4, in_1, xor_1_out);
  and and_2 (and_2_out, xor_1_out, in_1);
endmodule

module ULA_4_bits (
  input  B3,
  input  B2,
  input  B1,
  input  B0,
  input  A3,
  input  A2,
  input  A1,
  input  A0,
  input  Binvert,
  input  [1:0] OPS,
  output S0,
  output S1,
  output S2,
  output S3,
  output C_OUT
);

  wire ula_1_bit_1_carryout, ula_1_bit_2_carryout, ula_1_bit_3_carryout;

  ULA_1_bit ula_1_bit_1 (
    .A(A0), .B(B0), .Binvert(Binvert), .Carry_in(Binvert), .Operation(OPS), .CarryOut(ula_1_bit_1_carryout),
    .Result(S0));
  ULA_1_bit ula_1_bit_2 (
    .A(A1), .B(B1), .Binvert(Binvert), .Carry_in(ula_1_bit_1_carryout), .Operation(OPS),
    .CarryOut(ula_1_bit_2_carryout), .Result(S1));
  ULA_1_bit ula_1_bit_3 (
    .A(A2), .B(B2), .Binvert(Binvert), .Carry_in(ula_1_bit_2_carryout), .Operation(OPS),
    .CarryOut(ula_1_bit_3_carryout), .Result(S2));
  ULA_1_bit ula_1_bit_4 (
    .A(A3), .B(B3), .Binvert(Binvert), .Carry_in(ula_1_bit_3_carryout), .Operation(OPS), .CarryOut(C_OUT),
    .Result(S3));
endmodule
