// Logisim project ROMANELLI.circ as structural Verilog: 6 circuits, main circuit main
module main (
);

  // DisplayDecoder displaydecoder_1: pin names not known
  _7_Segment_Display u_7_segment_display_1 ();  // open: g, f, a, b, e, d, c, dp
endmodule

module meio_somador (
  input  A0,
  input  B0,
  output Soma,
  output Carru_out
);

  and and_1 (Carru_out, A0, B0);
  xor xor_1 (Soma, A0, B0);
endmodule

module somador_completo (
  input  CARRY_IN,
  input  A0,
  input  B0,
  output S0,
  output CARRY_OUT
);

  wire meio_somador_1_carru_out, meio_somador_1_soma, meio_somador_2_carru_out;

  meio_somador meio_somador_1 (.A0(A0), .B0(B0), .Carru_out(meio_somador_1_carru_out), .Soma(meio_somador_1_soma));
  meio_somador meio_somador_2 (
    .A0(CARRY_IN), .B0(meio_somador_1_soma), .Carru_out(meio_somador_2_carru_out), .Soma(S0));
  or or_1 (CARRY_OUT, meio_somador_1_carru_out, meio_somador_2_carru_out);
endmodule

module somador_de_4_bits (
  input  C_IN,
  input  a0,
  input  a1,
  input  a2,
  input  a3,
  input  b0,
  input  b1,
  input  b2,
  input  b3,
  input  C_OUT,
  output S0,
  output S1,
  output S2,
  output S3,
  output Overflow
);

  wire somador_completo_1_carry_out, somador_completo_2_carry_out, somador_completo_4_carry_out;

  somador_completo somador_completo_1 (
    .A0(a1), .B0(b1), .CARRY_IN(somador_completo_4_carry_out), .CARRY_OUT(somador_completo_1_carry_out),
    .S0(S1));
  somador_completo somador_completo_2 (
    .A0(a2), .B0(b2), .CARRY_IN(somador_completo_1_carry_out), .CARRY_OUT(somador_completo_2_carry_out),
    .S0(S2));
  somador_completo somador_completo_3 (
    .A0(a3), .B0(b3), .CARRY_IN(somador_completo_2_carry_out), .CARRY_OUT(C_OUT), .S0(S3));
  somador_completo somador_completo_4 (
    .A0(a0), .B0(b0), .CARRY_IN(C_IN), .CARRY_OUT(somador_completo_4_carry_out), .S0(S0));
  xor xor_1 (Overflow, somador_completo_2_carry_out, C_OUT);
endmodule

module decodificador (
  input  E3,
  input  E2,
  input  E1,
  input  E0,
  output A,
  output B,
  output C,
  output D,
  output E,
  output F,
  output G
);

  wire and_1_out, and_2_out, and_3_out, and_4_out, and_5_out, and_6_out, and_7_out, and_8_out, and_9_out,
       and_10_out, and_11_out, and_12_out, and_13_out, and_14_out, and_15_out, and_16_out, and_17_out,
       and_18_out, and_19_out, and_20_out, and_21_out, and_22_out, and_23_out, and_24_out, and_25_out,
       and_26_out, and_27_out, and_28_out, and_29_out, and_30_out, and_31_out, and_32_out, and_33_out,
       and_34_out, and_35_out, not_1_out, not_2_out, not_3_out, not_4_out, not_5_out, not_6_out, not_7_out,
       not_8_out, not_9_out, not_10_out, not_11_out, not_12_out, not_13_out, not_14_out, not_15_out,
       not_16_out, not_17_out, not_18_out, not_19_out, not_20_out, not_21_out, not_22_out, not_23_out,
       not_24_out, not_25_out, not_26_out, not_27_out, not_28_out, not_29_out, not_30_out, not_31_out,
       not_32_out, not_33_out, not_34_out, not_35_out, not_36_out, not_37_out, not_38_out, not_39_out,
       not_40_out, not_41_out, not_42_out, not_43_out;

  not not_1 (not_1_out, E2);
  and and_1 (and_1_out, not_1_out, not_2_out);
  not not_2 (not_2_out, E0);
  not not_3 (not_3_out, E3);
  and and_2 (and_2_out, not_3_out, E1);
  not not_4 (not_4_out, E3);
  and and_3 (and_3_out, not_4_out, E2, E0);
  and and_4 (and_4_out, E2, E1);
  not not_5 (not_5_out, E2);
  and and_5 (and_5_out, E3, not_5_out, not_6_out);
  not not_6 (not_6_out, E1);
  and and_6 (and_6_out, E3, not_7_out);
  not not_7 (not_7_out, E0);
  not not_8 (not_8_out, E3);
  and and_7 (and_7_out, not_8_out, not_9_out);
  not not_9 (not_9_out, E2);
  not not_10 (not_10_out, E3);
  not not_11 (not_11_out, E1);
  and and_8 (and_8_out, not_10_out, not_11_out, not_12_out);
  not not_12 (not_12_out, E0);
  not not_13 (not_13_out, E2);
  and and_9 (and_9_out, not_13_out, not_14_out);
  not not_14 (not_14_out, E0);
  not not_15 (not_15_out, E3);
  and and_10 (and_10_out, not_15_out, E1, E0);
  and and_11 (and_11_out, E3, not_16_out, E0);
  not not_16 (not_16_out, E1);
  not not_17 (not_17_out, E3);
  and and_12 (and_12_out, not_17_out, not_18_out);
  not not_18 (not_18_out, E1);
  not not_19 (not_19_out, E3);
  and and_13 (and_13_out, not_19_out, E0);
  not not_20 (not_20_out, E1);
  and and_14 (and_14_out, not_20_out, E0);
  not not_21 (not_21_out, E3);
  and and_15 (and_15_out, not_21_out, E2);
  and and_16 (and_16_out, E3, not_22_out);
  not not_22 (not_22_out, E2);
  not not_23 (not_23_out, E3);
  not not_24 (not_24_out, E2);
  and and_17 (and_17_out, not_23_out, not_24_out, not_25_out);
  not not_25 (not_25_out, E0);
  not not_26 (not_26_out, E2);
  and and_18 (and_18_out, not_26_out, E1, E0);
  and and_19 (and_19_out, E2, not_27_out, E0);
  not not_27 (not_27_out, E1);
  and and_20 (and_20_out, E2, E1, not_28_out);
  not not_28 (not_28_out, E0);
  and and_21 (and_21_out, E3, not_29_out);
  not not_29 (not_29_out, E1);
  not not_30 (not_30_out, E2);
  and and_22 (and_22_out, not_30_out, not_31_out);
  not not_31 (not_31_out, E0);
  and and_23 (and_23_out, E1, not_32_out);
  not not_32 (not_32_out, E0);
  and and_24 (and_24_out, E3, E1);
  and and_25 (and_25_out, E3, E2);
  not not_33 (not_33_out, E1);
  and and_26 (and_26_out, not_33_out, not_34_out);
  not not_34 (not_34_out, E0);
  not not_35 (not_35_out, E3);
  and and_27 (and_27_out, not_35_out, E2, not_36_out);
  not not_36 (not_36_out, E1);
  and and_28 (and_28_out, E2, not_37_out);
  not not_37 (not_37_out, E0);
  and and_29 (and_29_out, E3, not_38_out);
  not not_38 (not_38_out, E2);
  and and_30 (and_30_out, E3, E1);
  not not_39 (not_39_out, E2);
  and and_31 (and_31_out, not_39_out, E1);
  and and_32 (and_32_out, E1, not_40_out);
  not not_40 (not_40_out, E0);
  not not_41 (not_41_out, E3);
  and and_33 (and_33_out, not_41_out, E2, not_42_out);
  not not_42 (not_42_out, E1);
  and and_34 (and_34_out, E3, not_43_out);
  not not_43 (not_43_out, E2);
  and and_35 (and_35_out, E3, E0);
  or or_1 (B, and_7_out, and_8_out, and_9_out, and_10_out, and_11_out);
  or or_2 (C, and_12_out, and_13_out, and_14_out, and_15_out, and_16_out);
  or or_3 (D, and_17_out, and_18_out, and_19_out, and_20_out, and_21_out);
  or or_4 (E, and_22_out, and_23_out, and_24_out, and_25_out);
  or or_5 (F, and_26_out, and_27_out, and_28_out, and_29_out, and_30_out);
  or or_6 (G, and_31_out, and_32_out, and_33_out, and_34_out, and_35_out);
  or or_7 (A, and_1_out, and_2_out, and_3_out, and_4_out, and_5_out, and_6_out);
endmodule

module Calculadora (
  input  A0,
  input  Ci,
  input  A1,
  input  A2,
  input  A3,
  input  B0,
  input  B1,
  input  B2,
  input  B3,
  output S0,
  output S1,
  output S2,
  output S3,
  output Overflow,
  output Co
);

  wire Decodificador_2_a, Decodificador_2_b, Decodificador_2_c, Decodificador_2_d, Decodificador_2_e,
       Decodificador_2_f, Decodificador_2_g, Decodificador_3_a, Decodificador_3_b, Decodificador_3_c,
       Decodificador_3_d, Decodificador_3_e, Decodificador_3_f, Decodificador_3_g, Decodificador_a,
       Decodificador_b, Decodificador_c, Decodificador_d, Decodificador_e, Decodificador_f, Decodificador_g;

  decodificador Decodificador (
    .E3(A3), .E2(A2), .E1(A1), .E0(A0), .A(Decodificador_a), .B(Decodificador_b), .C(Decodificador_c),
    .D(Decodificador_d), .E(Decodificador_e), .F(Decodificador_f), .G(Decodificador_g));
  somador_de_4_bits somador_4_bits (
    .a0(A0), .a1(A1), .a2(A2), .a3(A3), .b0(B0), .b1(B1), .b2(B2), .b3(B3), .C_IN(Ci), .C_OUT(Co), .S0(S0),
    .S1(S1), .S2(S1), .S3(S3), .Overflow(Overflow));
  decodificador Decodificador_2 (
    .E3(B3), .E2(B2), .E1(B1), .E0(B0), .A(Decodificador_2_a), .B(Decodificador_2_b), .C(Decodificador_2_c),
    .D(Decodificador_2_d), .E(Decodificador_2_e), .F(Decodificador_2_f), .G(Decodificador_2_g));
  _7_Segment_Display u_7_segment_display_1 (
    .g(Decodificador_g), .f(Decodificador_f), .a(Decodificador_a), .b(Decodificador_b), .e(Decodificador_e),
    .d(Decodificador_d), .c(Decodificador_c));  // open: dp
  _7_Segment_Display u_7_segment_display_2 (
    .g(Decodificador_2_g), .f(Decodificador_2_f), .a(Decodificador_2_a), .b(Decodificador_2_b),
    .e(Decodificador_2_e), .d(Decodificador_2_d), .c(Decodificador_2_c));  // open: dp
  decodificador Decodificador_3 (
    .E3(S3), .E2(S1), .E1(S1), .E0(S0), .A(Decodificador_3_a), .B(Decodificador_3_b), .C(Decodificador_3_c),
    .D(Decodificador_3_d), .E(Decodificador_3_e), .F(Decodificador_3_f), .G(Decodificador_3_g));
  _7_Segment_Display u_7_segment_display_3 (
    .g(Decodificador_3_g), .f(Decodificador_3_f), .a(Decodificador_3_a), .b(Decodificador_3_b),
    .e(Decodificador_3_e), .d(Decodificador_3_d), .c(Decodificador_3_c));  // open: dp

  assign S2 = S1;
endmodule
