// Logisim project atividadsouruimcauaebom.circ as structural Verilog: 1 circuit, main circuit main
module main (
  input  [3:0] in_1,
  input  [3:0] in_2,
  input  [3:0] in_3,
  output [3:0] out_4
);

  wire [3:0] and_1_out, and_2_out, nand_1_out, nor_1_out, not_1_out, not_2_out, not_3_out, not_4_out,
       xor_1_out;

  assign not_1_out = ~in_2;  // NOT_Gate not_1, 4 bits wide
  assign not_2_out = ~in_1;  // NOT_Gate not_2, 4 bits wide
  assign not_3_out = ~in_2;  // NOT_Gate not_3, 4 bits wide
  assign and_1_out = not_1_out & in_1;  // AND_Gate and_1, 4 bits wide
  assign nand_1_out = ~(in_2 & in_2);  // NAND_Gate nand_1, 4 bits wide
  assign not_4_out = ~in_1;  // NOT_Gate not_4, 4 bits wide
  assign xor_1_out = in_2 ^ in_1;  // XOR_Gate xor_1, 4 bits wide
  assign and_2_out = in_2 & not_2_out;  // AND_Gate and_2, 4 bits wide
  assign nor_1_out = ~(in_2 | in_1);  // NOR_Gate nor_1, 4 bits wide
  Multiplexer #(.select(4), .width(4), .enable("false")) multiplexer_1 (
    .in0(not_3_out), .in1(nor_1_out), .in2(and_1_out), .in3(4'b0000), .in4(nand_1_out), .in5(not_4_out),
    .in6(xor_1_out), .in7(and_2_out), .out(out_4), .sel(in_3));  // open: in8, in9, in10, in11, in12, in13, in14, in15
endmodule
